# Fritzing sketch hello_world_v1 (saved by Fritzing 0.9.9b)
breadboards: 1

parts:
  M1 = Arduino Nano 33 IOT-tht
  R1 = Resistor [tolerance=±5% power=0.25 resistance=220 package=THT]
  LED1 = LED - 5mm [color="Red (633nm)" current=0.030 package="5 mm [THT]"]

nets:
  N1: M1.pin_13, M1.pin_18
  N2: M1.pin_14, M1.pin_19, LED1.cathode
  N3: M1.pin_20, R1.Pin_1
  N4: R1.Pin_0, LED1.anode

custom parts:
  Arduino Nano 33 IOT-tht: The Arduino Nano 33 IoT is the easiest and cheapest point of entry to enhance existing devices (and creating new ones) to be part of the IoT and designing pico-network applications. Whether you are looking at building a sensor network connected to your office or home router, or if you want to create a BLE device sending data to a cellphone, the Nano 33 IoT is your one-stop-solution for many of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
